// Logisim project Projeto_1.circ as structural Verilog: 3 circuits, main circuit main
module main (
  input  SW0,
  input  SW1,
  input  SEL,
  output LED0,
  output LED1
);

  wire mux2_1_1_s;

  Mux2_1 mux2_1_1 (.S(mux2_1_1_s), .Sel(SEL), .A(SW0), .B(SW1));
  Demux1_2 demux1_2_1 (.A(LED0), .B(LED1), .Sel(SEL), .Ent(mux2_1_1_s));
endmodule

module Mux2_1 (
  input  Sel,
  input  A,
  input  B,
  output S
);

  wire and_1_out, and_2_out, not_1_out;

  not not_1 (not_1_out, Sel);
  and and_1 (and_1_out, not_1_out, A);
  and and_2 (and_2_out, Sel, B);
  or or_1 (S, and_1_out, and_2_out);
endmodule

module Demux1_2 (
  input  Sel,
  input  Ent,
  output A,
  output B
);

  wire not_1_out;

  not not_1 (not_1_out, Sel);
  and and_1 (A, not_1_out, Ent);
  and and_2 (B, Sel, Ent);
endmodule
