// Logisim project Projeto_3.circ as structural Verilog: 4 circuits, main circuit main
module main (
  input  SW0,
  input  SW1,
  input  SEL,
  output LED0,
  output LED1
);

  wire BT0_out, BT1_out, BT2_out, mux2_1_1_s, voter_1_s, xor_1_out, xor_2_out, xor_3_out;

  Button BT0 (.out(BT0_out));
  Button BT1 (.out(BT1_out));
  Button BT2 (.out(BT2_out));
  Mux2_1 mux2_1_1 (.S(mux2_1_1_s), .Sel(SEL), .A(SW0), .B(SW1));
  xor xor_1 (xor_1_out, BT0_out, mux2_1_1_s);
  xor xor_2 (xor_2_out, BT1_out, mux2_1_1_s);
  xor xor_3 (xor_3_out, BT2_out, mux2_1_1_s);
  Voter voter_1 (.S(voter_1_s), .A(xor_1_out), .B(xor_2_out), .C(xor_3_out));
  Demux1_2 demux1_2_1 (.A(LED0), .B(LED1), .Sel(SEL), .Ent(voter_1_s));
endmodule

module Mux2_1 (
  input  Sel,
  input  A,
  input  B,
  output S
);

  wire and_1_out, and_2_out, not_1_out;

  not not_1 (not_1_out, Sel);
  and and_1 (and_1_out, not_1_out, A);
  and and_2 (and_2_out, Sel, B);
  or or_1 (S, and_1_out, and_2_out);
endmodule

module Demux1_2 (
  input  Sel,
  input  Ent,
  output A,
  output B
);

  wire not_1_out;

  not not_1 (not_1_out, Sel);
  and and_1 (A, not_1_out, Ent);
  and and_2 (B, Sel, Ent);
endmodule

module Voter (
  input  A,
  input  B,
  input  C,
  output S
);

  wire and_1_out, and_2_out, and_3_out, or_1_out;

  and and_1 (and_1_out, B, C);
  and and_2 (and_2_out, A, C);
  and and_3 (and_3_out, A, B);
  or or_1 (or_1_out, and_1_out, and_2_out);
  or or_2 (S, or_1_out, and_3_out);
endmodule
