// Logisim project Dualidade.circ as structural Verilog: 1 circuit, main circuit main
module main (
  input  A,
  input  B,
  input  C,
  input  A_2,
  input  A_4,
  input  B_4,
  input  C_4,
  input  A_3,
  input  B_3,
  output out_10,
  output out_11,
  output out_12,
  output out_13,
  output out_14,
  output out_15,
  output out_16,
  output out_17,
  output out_18,
  output out_19
);

  wire nand_2_out, nand_3_out, nand_4_out, nand_6_out, nand_7_out, nand_8_out, nand_9_out, nand_10_out,
       nand_11_out, nor_2_out, nor_3_out, nor_4_out, nor_8_out, nor_9_out, nor_10_out, nor_11_out,
       nor_12_out, nor_13_out, nor_14_out, nor_15_out, nor_16_out, nor_17_out, not_1_out;

  not not_1 (not_1_out, B);
  nand nand_1 (out_11, A_2, A_2);
  nand nand_2 (nand_2_out, A, not_1_out);
  nand nand_3 (nand_3_out, A_3, A_3);
  nand nand_4 (nand_4_out, B_3, B_3);
  nor nor_1 (out_14, A_3, A_3);
  nor nor_2 (nor_2_out, A_3, A_3);
  nor nor_3 (nor_3_out, B_3, B_3);
  nor nor_4 (nor_4_out, A_3, B_3);
  nor nor_5 (out_16, nor_2_out, nor_3_out);
  nor nor_6 (out_17, nor_4_out, nor_4_out);
  nor nor_7 (out_10, nand_2_out, C);
  nand nand_5 (out_13, nand_3_out, nand_4_out);
  nand nand_6 (nand_6_out, A_4, B_4);
  nand nand_7 (nand_7_out, A_4, B_4);
  nor nor_8 (nor_8_out, A_4, A_4);
  nor nor_9 (nor_9_out, B_4, B_4);
  nor nor_10 (nor_10_out, C_4, C_4);
  nor nor_11 (nor_11_out, A_4, A_4);
  nor nor_12 (nor_12_out, B_4, B_4);
  nand nand_8 (nand_8_out, nand_6_out, nand_6_out);
  nand nand_9 (nand_9_out, C_4, C_4);
  nor nor_13 (nor_13_out, nor_8_out, nor_9_out);
  nor nor_14 (nor_14_out, nor_10_out, nor_10_out);
  nor nor_15 (nor_15_out, nor_11_out, nor_12_out);
  nand nand_10 (nand_10_out, nand_8_out, nand_8_out);
  nand nand_11 (nand_11_out, nand_9_out, nand_9_out);
  nor nor_16 (nor_16_out, nor_13_out, nor_14_out);
  nor nor_17 (nor_17_out, nor_15_out, C_4);
  nand nand_12 (out_12, nand_10_out, nand_11_out);
  nand nand_13 (out_15, nand_7_out, C_4);
  nor nor_18 (out_18, nor_16_out, nor_16_out);
  nor nor_19 (out_19, nor_17_out, nor_17_out);
endmodule
