// Logisim project Exercicios_1.circ as structural Verilog: 5 circuits, main circuit questao_a
module questao_a (
  input  A_a,
  input  B_a,
  input  C_a,
  output out_4,
  output out_5,
  output out_6
);

  wire and_1_out, nand_1_out, nand_2_out, nand_3_out, nand_4_out, nand_5_out, nand_6_out, nand_7_out,
       nor_1_out, nor_2_out, nor_3_out, nor_4_out, nor_5_out, nor_6_out, or_1_out;

  or or_1 (or_1_out, A_a, B_a);
  nand nand_1 (nand_1_out, A_a, A_a);
  nand nand_2 (nand_2_out, B_a, B_a);
  nor nor_1 (nor_1_out, A_a, B_a);
  and and_1 (and_1_out, or_1_out, C_a);
  or or_2 (out_4, and_1_out, B_a);
  nand nand_3 (nand_3_out, nand_1_out, nand_2_out);
  nor nor_2 (nor_2_out, nor_1_out, nor_1_out);
  nand nand_4 (nand_4_out, nand_3_out, C_a);
  nor nor_3 (nor_3_out, nor_2_out, nor_2_out);
  nor nor_4 (nor_4_out, C_a, C_a);
  nand nand_5 (nand_5_out, nand_4_out, nand_4_out);
  nor nor_5 (nor_5_out, nor_3_out, nor_4_out);
  nand nand_6 (nand_6_out, nand_5_out, nand_5_out);
  nand nand_7 (nand_7_out, B_a, B_a);
  nor nor_6 (nor_6_out, nor_5_out, B_a);
  nand nand_8 (out_5, nand_6_out, nand_7_out);
  nor nor_7 (out_6, nor_6_out, nor_6_out);

  // Notes on the sheet:
  //   a) X = (A+B)C+B
  //   Normal
  //   NAND
  //   NOR
endmodule

module questao_b (
  input  A_b,
  input  B_b,
  input  C_b,
  output out_4,
  output out_5,
  output out_6,
  output out_7
);

  wire nand_1_out, nand_2_out, nand_3_out, nand_4_out, nand_5_out, nor_1_out, nor_2_out, nor_3_out,
       nor_4_out, nor_5_out, nor_6_out, nor_7_out, nor_8_out, not_1_out, or_1_out;

  or or_1 (or_1_out, A_b, B_b);
  nand nand_1 (nand_1_out, A_b, A_b);
  nand nand_2 (nand_2_out, B_b, B_b);
  nor nor_1 (nor_1_out, A_b, B_b);
  nor nor_2 (nor_2_out, A_b, B_b);
  not not_1 (not_1_out, or_1_out);
  nand nand_3 (nand_3_out, nand_1_out, nand_2_out);
  nor nor_3 (nor_3_out, nor_1_out, nor_1_out);
  nor nor_4 (nor_4_out, nor_2_out, nor_2_out);
  and and_1 (out_4, not_1_out, C_b);
  nand nand_4 (nand_4_out, nand_3_out, nand_3_out);
  nor nor_5 (nor_5_out, nor_3_out, nor_3_out);
  nand nand_5 (nand_5_out, nand_4_out, C_b);
  nor nor_6 (nor_6_out, nor_5_out, nor_5_out);
  nor nor_7 (nor_7_out, C_b, C_b);
  nor nor_8 (nor_8_out, C_b, C_b);
  nand nand_6 (out_5, nand_5_out, nand_5_out);
  nor nor_9 (out_6, nor_6_out, nor_7_out);
  nor nor_10 (out_7, nor_4_out, nor_8_out);

  // Notes on the sheet:
  //   b) X = (A+B)'C
  //   Normal
  //   NAND
  //   NOR
  //   NOR (Simplificado)
endmodule

module questao_c (
  input  in_1,
  input  c__X___AB_prime_C_AB,
  input  in_3,
  output out_4,
  output out_5,
  output out_6,
  output out_7
);

  wire and_1_out, and_2_out, nand_1_out, nand_2_out, nand_3_out, nand_4_out, nand_5_out, nand_6_out,
       nand_7_out, nand_8_out, nand_9_out, nand_10_out, nand_11_out, nand_12_out, nand_13_out, nand_14_out,
       nand_16_out, nand_17_out, nor_1_out, nor_2_out, nor_3_out, nor_4_out, nor_5_out, nor_6_out, nor_7_out,
       nor_8_out, nor_9_out, nor_10_out, nor_11_out, not_1_out;

  not not_1 (not_1_out, c__X___AB_prime_C_AB);
  and and_1 (and_1_out, in_1, not_1_out, in_3);
  and and_2 (and_2_out, in_1, c__X___AB_prime_C_AB);
  nand nand_1 (nand_1_out, c__X___AB_prime_C_AB, c__X___AB_prime_C_AB);
  nand nand_2 (nand_2_out, in_1, c__X___AB_prime_C_AB);
  nand nand_3 (nand_3_out, c__X___AB_prime_C_AB, c__X___AB_prime_C_AB);
  nand nand_4 (nand_4_out, in_1, c__X___AB_prime_C_AB);
  nor nor_1 (nor_1_out, in_1, in_1);
  nor nor_2 (nor_2_out, c__X___AB_prime_C_AB, c__X___AB_prime_C_AB);
  nor nor_3 (nor_3_out, in_1, in_1);
  nor nor_4 (nor_4_out, c__X___AB_prime_C_AB, c__X___AB_prime_C_AB);
  nand nand_5 (nand_5_out, in_1, nand_1_out);
  nand nand_6 (nand_6_out, in_1, nand_3_out);
  or or_1 (out_4, and_1_out, and_2_out);
  nand nand_7 (nand_7_out, nand_2_out, nand_2_out);
  nand nand_8 (nand_8_out, nand_4_out, nand_4_out);
  nor nor_5 (nor_5_out, nor_2_out, nor_2_out);
  nor nor_6 (nor_6_out, nor_3_out, nor_4_out);
  nand nand_9 (nand_9_out, nand_5_out, nand_5_out);
  nand nand_10 (nand_10_out, nand_6_out, nand_6_out);
  nor nor_7 (nor_7_out, nor_1_out, nor_5_out);
  nand nand_11 (nand_11_out, nand_9_out, in_3);
  nand nand_12 (nand_12_out, nand_10_out, in_3);
  nand nand_13 (nand_13_out, nand_8_out, nand_8_out);
  nor nor_8 (nor_8_out, nor_7_out, nor_7_out);
  nor nor_9 (nor_9_out, in_3, in_3);
  nand nand_14 (nand_14_out, nand_11_out, nand_11_out);
  nand nand_15 (out_6, nand_12_out, nand_13_out);
  nor nor_10 (nor_10_out, nor_8_out, nor_9_out);
  nand nand_16 (nand_16_out, nand_14_out, nand_14_out);
  nand nand_17 (nand_17_out, nand_7_out, nand_7_out);
  nor nor_11 (nor_11_out, nor_10_out, nor_6_out);
  nand nand_18 (out_5, nand_16_out, nand_17_out);
  nor nor_12 (out_7, nor_11_out, nor_11_out);

  // Notes on the sheet:
  //   Normal
  //   NAND
  //   NOR
  //   NAND (Simplificado)
endmodule

module questao_d (
  input  A_d,
  input  B_d,
  input  C_d,
  output out_4,
  output out_5,
  output out_6,
  output out_7
);

  wire nand_1_out, nand_2_out, nand_3_out, nand_4_out, nand_5_out, nand_6_out, nand_7_out, nand_8_out,
       nor_1_out, nor_2_out, nor_3_out, nor_4_out, nor_5_out, nor_6_out, nor_7_out, nor_8_out, nor_9_out,
       nor_10_out, not_1_out, or_1_out, or_2_out;

  or or_1 (or_1_out, A_d, B_d);
  not not_1 (not_1_out, A_d);
  or or_2 (or_2_out, not_1_out, B_d);
  nand nand_1 (nand_1_out, A_d, A_d);
  nand nand_2 (nand_2_out, B_d, B_d);
  nand nand_3 (nand_3_out, A_d, A_d);
  nor nor_1 (nor_1_out, A_d, B_d);
  nor nor_2 (nor_2_out, A_d, A_d);
  nor nor_3 (nor_3_out, A_d, B_d);
  nor nor_4 (nor_4_out, A_d, A_d);
  and and_1 (out_4, or_1_out, or_2_out);
  nand nand_4 (nand_4_out, nand_1_out, nand_2_out);
  nand nand_5 (nand_5_out, nand_3_out, nand_3_out);
  nand nand_6 (nand_6_out, B_d, B_d);
  nor nor_5 (nor_5_out, nor_1_out, nor_1_out);
  nor nor_6 (nor_6_out, nor_2_out, B_d);
  nor nor_7 (nor_7_out, nor_4_out, B_d);
  nor nor_8 (nor_8_out, nor_5_out, nor_5_out);
  nor nor_9 (nor_9_out, nor_6_out, nor_6_out);
  nand nand_7 (nand_7_out, nand_5_out, nand_6_out);
  nor nor_10 (nor_10_out, nor_9_out, nor_9_out);
  nand nand_8 (nand_8_out, nand_4_out, nand_7_out);
  nor nor_11 (out_6, nor_8_out, nor_10_out);
  nor nor_12 (out_7, nor_3_out, nor_7_out);
  nand nand_9 (out_5, nand_8_out, nand_8_out);

  // Notes on the sheet:
  //   d) X = (A+B)(A'+B)
  //   Normal
  //   NAND
  //   NOR
  //   NOR (Simplificado)
endmodule

module questao_e (
  input  A_e,
  input  B_e,
  input  C_e,
  output out_4,
  output out_5,
  output out_6,
  output out_7,
  output out_8
);

  wire and_1_out, nand_1_out, nand_2_out, nand_3_out, nand_4_out, nand_5_out, nand_6_out, nand_7_out,
       nand_8_out, nand_9_out, nand_10_out, nand_11_out, nand_12_out, nand_13_out, nand_14_out, nand_15_out,
       nand_16_out, nor_1_out, nor_2_out, nor_3_out, nor_4_out, nor_5_out, nor_6_out, nor_7_out, nor_8_out,
       nor_9_out, nor_10_out, nor_11_out, nor_12_out, nor_13_out, nor_14_out, nor_15_out, nor_16_out,
       nor_17_out, nor_18_out, not_1_out, not_2_out, or_1_out, or_2_out;

  not not_1 (not_1_out, B_e);
  not not_2 (not_2_out, C_e);
  and and_1 (and_1_out, B_e, C_e);
  or or_1 (or_1_out, not_1_out, not_2_out);
  nand nand_1 (nand_1_out, A_e, A_e);
  nand nand_2 (nand_2_out, B_e, C_e);
  nand nand_3 (nand_3_out, B_e, B_e);
  nand nand_4 (nand_4_out, C_e, C_e);
  nand nand_5 (nand_5_out, A_e, A_e);
  nand nand_6 (nand_6_out, B_e, C_e);
  nor nor_1 (nor_1_out, B_e, B_e);
  nor nor_2 (nor_2_out, C_e, C_e);
  nor nor_3 (nor_3_out, B_e, B_e);
  nor nor_4 (nor_4_out, C_e, C_e);
  nor nor_5 (nor_5_out, B_e, B_e);
  nor nor_6 (nor_6_out, C_e, C_e);
  nor nor_7 (nor_7_out, B_e, B_e);
  nor nor_8 (nor_8_out, C_e, C_e);
  or or_2 (or_2_out, A_e, and_1_out);
  nand nand_7 (nand_7_out, nand_2_out, nand_2_out);
  nand nand_8 (nand_8_out, nand_3_out, nand_3_out);
  nand nand_9 (nand_9_out, nand_4_out, nand_4_out);
  nor nor_9 (nor_9_out, nor_1_out, nor_2_out);
  nor nor_10 (nor_10_out, nor_3_out, nor_4_out);
  nor nor_11 (nor_11_out, nor_5_out, nor_6_out);
  nor nor_12 (nor_12_out, nor_7_out, nor_8_out);
  and and_2 (out_4, or_2_out, or_1_out);
  nand nand_10 (nand_10_out, nand_7_out, nand_7_out);
  nand nand_11 (nand_11_out, nand_8_out, nand_9_out);
  nand nand_12 (nand_12_out, B_e, C_e);
  nor nor_13 (nor_13_out, A_e, nor_9_out);
  nor nor_14 (nor_14_out, nor_10_out, nor_10_out);
  nor nor_15 (nor_15_out, A_e, nor_11_out);
  nand nand_13 (nand_13_out, nand_1_out, nand_10_out);
  nand nand_14 (nand_14_out, nand_5_out, nand_6_out);
  nor nor_16 (nor_16_out, nor_13_out, nor_13_out);
  nor nor_17 (nor_17_out, nor_14_out, nor_14_out);
  nand nand_15 (nand_15_out, nand_13_out, nand_11_out);
  nand nand_16 (nand_16_out, nand_14_out, nand_12_out);
  nand nand_17 (out_5, nand_15_out, nand_15_out);
  nand nand_18 (out_6, nand_16_out, nand_16_out);
  nor nor_18 (nor_18_out, nor_16_out, nor_16_out);
  nor nor_19 (out_7, nor_18_out, nor_17_out);
  nor nor_20 (out_8, nor_15_out, nor_12_out);

  // Notes on the sheet:
  //   e) X = (A+BC)(B'+C')
  //   NOR
  //   Normal
  //   NAND
  //   NAND (Simplificado)
  //   NOR (Simplificado)
endmodule
