// Logisim project Flip_Flop.circ as structural Verilog: 4 circuits, main circuit main
module main (
  input  Se,
  input  E,
  input  D,
  output Q
);

  wire mux_2_1_1_r;

  Mux_2_1 mux_2_1_1 (.R(mux_2_1_1_r), .A(Q), .B(E), .Se(Se));
  Flip_Flop_D flip_flop_d_1 (.Q(Q), .D(mux_2_1_1_r), .Clk(D));
endmodule

module Flip_Flop_D (
  input  D,
  input  Clk,
  output Q
);

  wire latch_d_1_q, not_1_out;

  not not_1 (not_1_out, Clk);
  Latch_D latch_d_1 (.Q(latch_d_1_q), .Clk(not_1_out), .D(D));
  Latch_D latch_d_2 (.Q(Q), .Clk(Clk), .D(latch_d_1_q));
endmodule

module Latch_D (
  input  D,
  input  Clk,
  output Q
);

  wire and_1_out, and_2_out, nor_1_out, not_1_out;

  not not_1 (not_1_out, D);
  and and_1 (and_1_out, D, Clk);
  and and_2 (and_2_out, Clk, not_1_out);
  nor nor_1 (nor_1_out, and_1_out, Q);
  nor nor_2 (Q, nor_1_out, and_2_out);
endmodule

module Mux_2_1 (
  input  Se,
  input  A,
  input  B,
  output R
);

  wire and_1_out, and_2_out, not_1_out;

  not not_1 (not_1_out, Se);
  and and_1 (and_1_out, not_1_out, A);
  and and_2 (and_2_out, Se, B);
  or or_1 (R, and_1_out, and_2_out);
endmodule
