// Logisim project Multiplexador.circ as structural Verilog: 5 circuits, main circuit main
module main (
  input  A,
  input  B,
  output out_3,
  output out_4
);

  Soma_1bit soma_1bit_1 (.A(A), .B(B), .D(out_3), .U(out_4));
endmodule

module Demux (
  input  Sel,
  input  E,
  output out_3,
  output out_4
);

  wire not_1_out;

  not not_1 (not_1_out, Sel);
  and and_1 (out_3, not_1_out, E);
  and and_2 (out_4, Sel, E);
endmodule

module Mux (
  input  Sel,
  input  A,
  input  B,
  output out_4
);

  wire and_1_out, and_2_out, not_1_out;

  not not_1 (not_1_out, Sel);
  and and_1 (and_1_out, not_1_out, A);
  and and_2 (and_2_out, Sel, B);
  or or_1 (out_4, and_1_out, and_2_out);
endmodule

module Soma_1bit (
  input  A,
  input  B,
  output D,
  output U
);

  wire not_1_out;

  and and_1 (D, A, B);
  and and_2 (U, A, not_1_out);
  not not_1 (not_1_out, B);
endmodule

module Soma_2bit (
  input  [1:0] A,
  input  [1:0] B
);

  // AND_Gate and_1 is placed but not wired
endmodule
