// Logisim project Multplexador_v2.circ as structural Verilog
module Mux2_1 (
  input  Se,
  input  A,
  input  B,
  output R
);

  wire and_1_out, and_2_out, not_1_out;

  not not_1 (not_1_out, Se);
  and and_1 (and_1_out, not_1_out, A);
  and and_2 (and_2_out, Se, B);
  or or_1 (R, and_1_out, and_2_out);
endmodule

module Mux4_1 (
  input  [1:0] Se,
  input  A,
  input  B,
  input  C,
  input  D,
  output Saida
);

  wire mux2_1_1_r, mux2_1_2_r;

  Mux2_1 mux2_1_1 (.R(mux2_1_1_r), .A(A), .B(B), .Se(Se[1]));
  Mux2_1 mux2_1_2 (.R(mux2_1_2_r), .A(C), .B(D), .Se(Se[1]));
  Mux2_1 mux2_1_3 (.R(Saida), .A(mux2_1_1_r), .B(mux2_1_2_r), .Se(Se[0]));
endmodule

module Demux (
  input  Sel,
  input  E,
  output out_3,
  output out_4
);

  wire not_1_out;

  not not_1 (not_1_out, Sel);
  and and_1 (out_3, not_1_out, E);
  and and_2 (out_4, Sel, E);
endmodule

module Mux (
  input  Sel,
  input  A,
  input  B,
  output out_4
);

  wire and_1_out, and_2_out, not_1_out;

  not not_1 (not_1_out, Sel);
  and and_1 (and_1_out, not_1_out, A);
  and and_2 (and_2_out, Sel, B);
  or or_1 (out_4, and_1_out, and_2_out);
endmodule

module Soma_1bit (
  input  A,
  input  B,
  output D,
  output U
);

  wire not_1_out;

  and and_1 (D, A, B);
  and and_2 (U, A, not_1_out);
  not not_1 (not_1_out, B);
endmodule

module Soma_2bit (
  input  [1:0] A,
  input  [1:0] B
);

  // AND_Gate and_1 is placed but not wired
endmodule

module Latch_D (
  input  Clk,
  output Q
);

  wire and_1_out, and_2_out, button_1_out, nor_1_out, not_1_out;

  Button button_1 (.out(button_1_out));
  not not_1 (not_1_out, button_1_out);
  and and_1 (and_1_out, button_1_out, Clk);
  and and_2 (and_2_out, Clk, not_1_out);
  nor nor_1 (nor_1_out, and_1_out, Q);
  nor nor_2 (Q, nor_1_out, and_2_out);
endmodule
