// Logisim project Projeto_Final_Parte_2.circ as structural Verilog: 16 circuits, main circuit main
module main (
  input  [1:0] Sel_Operation,
  input  [2:0] Sel_Read_A,
  input  [2:0] Sel_Read_B,
  input  Sel_Data_In,
  input  [7:0] Data_In,
  input  [2:0] Sel_Write,
  input  Write,
  input  Clock,
  output [7:0] Data_Out
);

  wire [7:0] mux_2_1_8b_1_s, part_1_1_data_out_a, part_1_1_data_out_b;

  Mux_2_1_8b mux_2_1_8b_1 (.S(mux_2_1_8b_1_s), .Sel(Sel_Data_In), .A(Data_In), .B(Data_Out));
  Part_1 part_1_1 (
    .Data_Out_A(part_1_1_data_out_a), .Data_Out_B(part_1_1_data_out_b), .Write(Write), .Clock(Clock),
    .Sel_Read_A(Sel_Read_A), .Sel_Read_B(Sel_Read_B), .Sel_Write(Sel_Write), .Data_In(mux_2_1_8b_1_s));
  ULA ula_1 (
    .Data_Out(Data_Out), .Sel(Sel_Operation), .Data_In_A(part_1_1_data_out_a), .Data_In_B(part_1_1_data_out_b));

  // Notes on the sheet:
  //   Sel Options:
  //   00 - AND
  //   01 - OR
  //   10 - SUM
  //   11 - Subtraction
endmodule

module Latch_D (
  input  D,
  input  Clk,
  output Q
);

  wire and_1_out, and_2_out, nor_1_out, not_1_out;

  not not_1 (not_1_out, D);
  and and_1 (and_1_out, D, Clk);
  and and_2 (and_2_out, Clk, not_1_out);
  nor nor_1 (nor_1_out, and_1_out, Q);
  nor nor_2 (Q, nor_1_out, and_2_out);

  // Notes on the sheet:
  //   This inversor is used to avoid 11
  //   The main purpose of this circuit is to store a value in memory, like a RAM Memory
  //   The Final 2 XOR intercaleted will keep the values changing so that you can avoid getting the circuit "stuck" in only 1
endmodule

module FlipFlop_D (
  input  D,
  input  Clk,
  output Q
);

  wire latch_d_1_q, not_1_out;

  not not_1 (not_1_out, Clk);
  Latch_D latch_d_1 (.Q(latch_d_1_q), .D(D), .Clk(not_1_out));
  Latch_D latch_d_2 (.Q(Q), .D(latch_d_1_q), .Clk(Clk));

  // Notes on the sheet:
  //   Master
  //   2 Latch_D with one Clock
  //   If Clk == 0, load the Master Q, and Slave maintain the old value
  //   else If Clk == 0, load the Slave Q, and Master keeps the old value
  //   Slave
endmodule

module Reg_8 (
  input  [7:0] D,
  input  Write,
  input  Clk,
  output [7:0] Q
);

  FlipFlop_DEn flipflop_den_1 (.Q(Q[7]), .D(D[7]), .Clk(Clk), .En(Write));
  FlipFlop_DEn flipflop_den_2 (.Q(Q[6]), .D(D[6]), .Clk(Clk), .En(Write));
  FlipFlop_DEn flipflop_den_3 (.Q(Q[5]), .D(D[5]), .Clk(Clk), .En(Write));
  FlipFlop_DEn flipflop_den_4 (.Q(Q[4]), .D(D[4]), .Clk(Clk), .En(Write));
  FlipFlop_DEn flipflop_den_5 (.Q(Q[3]), .D(D[3]), .Clk(Clk), .En(Write));
  FlipFlop_DEn flipflop_den_6 (.Q(Q[2]), .D(D[2]), .Clk(Clk), .En(Write));
  FlipFlop_DEn flipflop_den_7 (.Q(Q[1]), .D(D[1]), .Clk(Clk), .En(Write));
  FlipFlop_DEn flipflop_den_8 (.Q(Q[0]), .D(D[0]), .Clk(Clk), .En(Write));

  // Notes on the sheet:
  //   Multiple Flip_Flop_Den storing one Clock Signal
  //   Each FlipFlop will store the value of 1 bit of the Register. And the values will only be stored in memory if the Write == 1
endmodule

module FlipFlop_DEn (
  input  En,
  input  D,
  input  Clk,
  output Q
);

  wire mux_2_1_2b_1_s;

  Mux_2_1_2b mux_2_1_2b_1 (.S(mux_2_1_2b_1_s), .A(Q), .B(D), .Se(En));
  FlipFlop_D flipflop_d_1 (.Q(Q), .D(mux_2_1_2b_1_s), .Clk(Clk));

  // Notes on the sheet:
  //   If the En == 1, then the value to be stored will be the D value
  //   else it will use the value stored in the memory of Q (FlipFlop_D)
endmodule

module Mux_2_1_2b (
  input  A,
  input  Se,
  input  B,
  output S
);

  wire and_1_out, and_2_out, not_1_out;

  not not_1 (not_1_out, Se);
  and and_1 (and_1_out, A, not_1_out);
  and and_2 (and_2_out, Se, B);
  or or_1 (S, and_1_out, and_2_out);

  // Notes on the sheet:
  //   If Se == 0, show Value of A
  //   else show value of B
  //   S = Sel'A+SelB
endmodule

module Sel_Reg (
  input  Wri,
  input  [2:0] Sel,
  output Reg_0,
  output Reg_1,
  output Reg_2,
  output Reg_3,
  output Reg_4,
  output Reg_5,
  output Reg_6,
  output Reg_7
);

  wire and_1_out, and_2_out, and_3_out, and_4_out, and_5_out, and_6_out, and_7_out, and_8_out, and_9_out,
       and_10_out, and_11_out, and_12_out, and_13_out, and_14_out, and_15_out, and_16_out;

  and and_1 (and_1_out, Wri, ~Sel[2]);  // AND_Gate
  and and_2 (and_2_out, Wri, ~Sel[2]);  // AND_Gate
  and and_3 (and_3_out, Wri, ~Sel[2]);  // AND_Gate
  and and_4 (and_4_out, Wri, ~Sel[2]);  // AND_Gate
  and and_5 (and_5_out, Wri, Sel[2]);
  and and_6 (and_6_out, Wri, Sel[2]);
  and and_7 (and_7_out, Wri, Sel[2]);
  and and_8 (and_8_out, Wri, Sel[2]);
  and and_9 (and_9_out, and_1_out, ~Sel[1]);  // AND_Gate
  and and_10 (and_10_out, and_2_out, ~Sel[1]);  // AND_Gate
  and and_11 (and_11_out, and_3_out, Sel[1]);
  and and_12 (and_12_out, and_4_out, Sel[1]);
  and and_13 (and_13_out, and_5_out, ~Sel[1]);  // AND_Gate
  and and_14 (and_14_out, and_6_out, ~Sel[1]);  // AND_Gate
  and and_15 (and_15_out, and_7_out, Sel[1]);
  and and_16 (and_16_out, and_8_out, Sel[1]);
  and and_17 (Reg_0, and_9_out, ~Sel[0]);  // AND_Gate
  and and_18 (Reg_1, and_10_out, Sel[0]);
  and and_19 (Reg_2, and_11_out, ~Sel[0]);  // AND_Gate
  and and_20 (Reg_3, and_12_out, Sel[0]);
  and and_21 (Reg_4, and_13_out, ~Sel[0]);  // AND_Gate
  and and_22 (Reg_5, and_14_out, Sel[0]);
  and and_23 (Reg_6, and_15_out, ~Sel[0]);  // AND_Gate
  and and_24 (Reg_7, and_16_out, Sel[0]);

  // Notes on the sheet:
  //   Since there is an output to every possibility in this circuit, you must add the number position for the Register you want 
  //   There must be a way to make this better -.-
  //   Using a Sum circuit, maybe?
endmodule

module Reg_Bank (
  input  Write,
  input  [2:0] Sel,
  input  [7:0] DATA_IN,
  input  Clk,
  output [7:0] out_5,
  output [7:0] out_6,
  output [7:0] out_7,
  output [7:0] out_8,
  output [7:0] out_9,
  output [7:0] out_10,
  output [7:0] out_11,
  output [7:0] out_12
);

  wire sel_reg_1_reg_0, sel_reg_1_reg_1, sel_reg_1_reg_2, sel_reg_1_reg_3, sel_reg_1_reg_4, sel_reg_1_reg_5,
       sel_reg_1_reg_6, sel_reg_1_reg_7;

  Sel_Reg sel_reg_1 (
    .Reg_0(sel_reg_1_reg_0), .Reg_1(sel_reg_1_reg_1), .Reg_2(sel_reg_1_reg_2), .Reg_3(sel_reg_1_reg_3),
    .Reg_4(sel_reg_1_reg_4), .Reg_5(sel_reg_1_reg_5), .Reg_6(sel_reg_1_reg_6), .Reg_7(sel_reg_1_reg_7),
    .Sel(Sel), .Wri(Write));
  Reg_8 reg_8_1 (.Q(out_12), .Write(sel_reg_1_reg_7), .Clk(Clk), .D(DATA_IN));
  Reg_8 reg_8_2 (.Q(out_11), .Write(sel_reg_1_reg_6), .Clk(Clk), .D(DATA_IN));
  Reg_8 reg_8_3 (.Q(out_10), .Write(sel_reg_1_reg_5), .Clk(Clk), .D(DATA_IN));
  Reg_8 reg_8_4 (.Q(out_9), .Write(sel_reg_1_reg_4), .Clk(Clk), .D(DATA_IN));
  Reg_8 reg_8_5 (.Q(out_8), .Write(sel_reg_1_reg_3), .Clk(Clk), .D(DATA_IN));
  Reg_8 reg_8_6 (.Q(out_7), .Write(sel_reg_1_reg_2), .Clk(Clk), .D(DATA_IN));
  Reg_8 reg_8_7 (.Q(out_6), .Write(sel_reg_1_reg_1), .Clk(Clk), .D(DATA_IN));
  Reg_8 reg_8_8 (.Q(out_5), .Write(sel_reg_1_reg_0), .Clk(Clk), .D(DATA_IN));

  // Notes on the sheet:
  //   The Circuit that will select the wanted Register
  //   7
  //   6
  //   5
  //   4
  //   Each Register will hold the value of 8 bits to be attached to their own output
  //   3
  //   2
  //   1
  //   0
  //   Reg_0
  //   Reg_1
  //   Reg_2
  //   Reg_3
  //   Reg_4
  //   Reg_5
  //   Reg_6
  //   Reg_7
endmodule

module Mux_2_1_8b (
  input  Sel,
  input  [7:0] A,
  input  [7:0] B,
  output [7:0] S
);

  Mux_2_1_2b mux_2_1_2b_1 (.S(S[0]), .A(A[0]), .B(B[0]), .Se(Sel));
  Mux_2_1_2b mux_2_1_2b_2 (.S(S[1]), .A(A[1]), .B(B[1]), .Se(Sel));
  Mux_2_1_2b mux_2_1_2b_3 (.S(S[2]), .A(A[2]), .B(B[2]), .Se(Sel));
  Mux_2_1_2b mux_2_1_2b_4 (.S(S[3]), .A(A[3]), .B(B[3]), .Se(Sel));
  Mux_2_1_2b mux_2_1_2b_5 (.S(S[4]), .A(A[4]), .B(B[4]), .Se(Sel));
  Mux_2_1_2b mux_2_1_2b_6 (.S(S[5]), .A(A[5]), .B(B[5]), .Se(Sel));
  Mux_2_1_2b mux_2_1_2b_7 (.S(S[6]), .A(A[6]), .B(B[6]), .Se(Sel));
  Mux_2_1_2b mux_2_1_2b_8 (.S(S[7]), .A(A[7]), .B(B[7]), .Se(Sel));

  // Notes on the sheet:
  //   Bit_0
  //   Bit_1
  //   Bit_2
  //   Bit_3
  //   Bit_4
  //   Bit_5
  //   Bit_6
  //   Bit_7
  //   Basically since it's the same Sel, the final 8 bits will be of the desired value
  //   A bunch of 2 bits Mux, that will define the value of the S by using the same Sel for all the Mux
endmodule

module Mux_8_1_8b (
  input  [2:0] Sel,
  input  [7:0] D_0,
  input  [7:0] D_1,
  input  [7:0] D_2,
  input  [7:0] D_3,
  input  [7:0] D_4,
  input  [7:0] D_5,
  input  [7:0] D_6,
  input  [7:0] D_7,
  output [7:0] D_Out
);

  wire [7:0] mux_2_1_8b_1_s, mux_2_1_8b_2_s, mux_2_1_8b_3_s, mux_2_1_8b_4_s, mux_2_1_8b_5_s, mux_2_1_8b_6_s;

  Mux_2_1_8b mux_2_1_8b_1 (.S(mux_2_1_8b_1_s), .Sel(Sel[0]), .A(D_0), .B(D_1));
  Mux_2_1_8b mux_2_1_8b_2 (.S(mux_2_1_8b_2_s), .Sel(Sel[0]), .A(D_2), .B(D_3));
  Mux_2_1_8b mux_2_1_8b_3 (.S(mux_2_1_8b_3_s), .Sel(Sel[0]), .A(D_4), .B(D_5));
  Mux_2_1_8b mux_2_1_8b_4 (.S(mux_2_1_8b_4_s), .Sel(Sel[0]), .A(D_6), .B(D_7));
  Mux_2_1_8b mux_2_1_8b_5 (.S(mux_2_1_8b_5_s), .Sel(Sel[1]), .A(mux_2_1_8b_1_s), .B(mux_2_1_8b_2_s));
  Mux_2_1_8b mux_2_1_8b_6 (.S(mux_2_1_8b_6_s), .Sel(Sel[1]), .A(mux_2_1_8b_3_s), .B(mux_2_1_8b_4_s));
  Mux_2_1_8b mux_2_1_8b_7 (.S(D_Out), .Sel(Sel[2]), .A(mux_2_1_8b_5_s), .B(mux_2_1_8b_6_s));

  // Notes on the sheet:
  //   The Sel will be number of the Data that you want
  //   The order in which each D_x is defined is important
  //   Each "Layer" of the Mux_2_1 will reduce the amount of possible data that you want
endmodule

module Sum_Unit (
  input  A,
  input  B,
  output C_Out,
  output S
);

  wire and_2_out, and_3_out, not_1_out, not_2_out;

  not not_1 (not_1_out, A);
  not not_2 (not_2_out, B);
  and and_1 (C_Out, A, B);
  and and_2 (and_2_out, not_1_out, B);
  and and_3 (and_3_out, A, not_2_out);
  or or_1 (S, and_2_out, and_3_out);

  // Notes on the sheet:
  //   S is the value of the current circuit
  //   C_Out is the output to be used in the C_In of another Circuit
endmodule

module Sum_Complete (
  input  C_In,
  input  A,
  input  B,
  output C_Out,
  output S
);

  wire and_1_out, and_2_out, and_3_out, and_4_out, and_5_out, and_6_out, and_7_out, not_1_out, not_2_out,
       not_3_out, not_4_out, not_5_out, not_6_out;

  not not_1 (not_1_out, C_In);
  not not_2 (not_2_out, B);
  not not_3 (not_3_out, C_In);
  not not_4 (not_4_out, A);
  not not_5 (not_5_out, A);
  not not_6 (not_6_out, B);
  and and_1 (and_1_out, C_In, A);
  and and_2 (and_2_out, C_In, B);
  and and_3 (and_3_out, A, B);
  and and_4 (and_4_out, not_1_out, A, not_2_out);
  and and_5 (and_5_out, not_3_out, not_4_out, B);
  and and_6 (and_6_out, C_In, A, B);
  and and_7 (and_7_out, C_In, not_5_out, not_6_out);
  or or_1 (C_Out, and_1_out, and_2_out, and_3_out);
  or or_2 (S, and_4_out, and_5_out, and_6_out, and_7_out);

  // Notes on the sheet:
  //   C_In is an extra result value of an privious circuit
  //   S is the value of the current circuit
  //   C_Out is the output to be used in the C_In of another Circuit
endmodule

module Sum_Subtraction_8b (
  input  [7:0] Data_In_A,
  input  [7:0] Data_In_B,
  input  Sel,
  output C_Out,
  output [7:0] Data_Out
);

  wire sum_complete_2_c_out, sum_complete_3_c_out, sum_complete_4_c_out, sum_complete_5_c_out,
       sum_complete_6_c_out, sum_complete_7_c_out, sum_complete_8_c_out, xor_2b_1_s, xor_2b_2_s, xor_2b_3_s,
       xor_2b_4_s, xor_2b_5_s, xor_2b_6_s, xor_2b_7_s, xor_2b_8_s;

  Sum_Complete sum_complete_1 (
    .C_Out(C_Out), .S(Data_Out[7]), .C_In(sum_complete_2_c_out), .A(Data_In_A[7]), .B(xor_2b_1_s));
  XOR_2b xor_2b_1 (.S(xor_2b_1_s), .A(Sel), .B(Data_In_B[7]));
  Sum_Complete sum_complete_2 (
    .C_Out(sum_complete_2_c_out), .S(Data_Out[6]), .C_In(sum_complete_3_c_out), .A(Data_In_A[6]),
    .B(xor_2b_2_s));
  XOR_2b xor_2b_2 (.S(xor_2b_2_s), .A(Sel), .B(Data_In_B[6]));
  Sum_Complete sum_complete_3 (
    .C_Out(sum_complete_3_c_out), .S(Data_Out[5]), .C_In(sum_complete_4_c_out), .A(Data_In_A[5]),
    .B(xor_2b_3_s));
  XOR_2b xor_2b_3 (.S(xor_2b_3_s), .A(Sel), .B(Data_In_B[5]));
  Sum_Complete sum_complete_4 (
    .C_Out(sum_complete_4_c_out), .S(Data_Out[4]), .C_In(sum_complete_5_c_out), .A(Data_In_A[4]),
    .B(xor_2b_4_s));
  XOR_2b xor_2b_4 (.S(xor_2b_4_s), .A(Sel), .B(Data_In_B[4]));
  Sum_Complete sum_complete_5 (
    .C_Out(sum_complete_5_c_out), .S(Data_Out[3]), .C_In(sum_complete_6_c_out), .A(Data_In_A[3]),
    .B(xor_2b_5_s));
  XOR_2b xor_2b_5 (.S(xor_2b_5_s), .A(Sel), .B(Data_In_B[3]));
  Sum_Complete sum_complete_6 (
    .C_Out(sum_complete_6_c_out), .S(Data_Out[2]), .C_In(sum_complete_7_c_out), .A(Data_In_A[2]),
    .B(xor_2b_6_s));
  XOR_2b xor_2b_6 (.S(xor_2b_6_s), .A(Sel), .B(Data_In_B[2]));
  Sum_Complete sum_complete_7 (
    .C_Out(sum_complete_7_c_out), .S(Data_Out[1]), .C_In(sum_complete_8_c_out), .A(Data_In_A[1]),
    .B(xor_2b_7_s));
  XOR_2b xor_2b_7 (.S(xor_2b_7_s), .A(Sel), .B(Data_In_B[1]));
  Sum_Complete sum_complete_8 (
    .C_Out(sum_complete_8_c_out), .S(Data_Out[0]), .C_In(Sel), .A(Data_In_A[0]), .B(xor_2b_8_s));
  XOR_2b xor_2b_8 (.S(xor_2b_8_s), .A(Sel), .B(Data_In_B[0]));

  // Notes on the sheet:
  //   8 bits == 255
  //   Sel will determine if it's a Sum (0) or Substraction (1)
  //   This C_Out is the leftover bit result of the calculation
  //   It may be added to the final result if you wish
  //   In the substraction you need to use "Complement of 2"
  //   Which means you must invert the bits of the Data_In_B
  //   And add 1 bit and the far right to the first Sum_Full
  //   The Sum_Subctraction circuit is a bunch of Sum_Complete and one Sum_Unit, equivalent to the amount of bits you want to calculate
  //   If Sel == 1, it will add the a bit for the "Complement of 2" to the C_In
endmodule

module ULA (
  input  [7:0] Data_In_A,
  input  [7:0] Data_In_B,
  input  [1:0] Sel,
  output [7:0] Data_Out
);

  wire [7:0] and_1_out, mux_2_1_8b_1_s, or_1_out, sum_subtraction_8b_1_data_out;

  assign and_1_out = Data_In_A & Data_In_B;  // AND_Gate and_1, 8 bits wide
  assign or_1_out = Data_In_A | Data_In_B;  // OR_Gate or_1, 8 bits wide
  Sum_Subtraction_8b sum_subtraction_8b_1 (
    .Data_Out(sum_subtraction_8b_1_data_out), .Sel(Sel[0]), .Data_In_B(Data_In_B), .Data_In_A(Data_In_A));  // open: C_Out
  Mux_2_1_8b mux_2_1_8b_1 (.S(mux_2_1_8b_1_s), .Sel(Sel[0]), .A(and_1_out), .B(or_1_out));
  Mux_2_1_8b mux_2_1_8b_2 (.S(Data_Out), .Sel(Sel[1]), .A(mux_2_1_8b_1_s), .B(sum_subtraction_8b_1_data_out));

  // Notes on the sheet:
  //   Sel Options:
  //   00 - AND
  //   01 - OR
  //   10 - SUM
  //   11 - Subtraction
  //   Since we're using a Register of 8 Bits, the C_Out will not be used in this circuit
endmodule

module XOR_2b (
  input  A,
  input  B,
  output S
);

  wire and_1_out, and_2_out, not_1_out, not_2_out;

  not not_1 (not_1_out, A);
  not not_2 (not_2_out, B);
  and and_1 (and_1_out, not_1_out, B);
  and and_2 (and_2_out, A, not_2_out);
  or or_1 (S, and_1_out, and_2_out);
endmodule

module Part_1 (
  input  [2:0] Sel_Read_A,
  input  [2:0] Sel_Read_B,
  input  [2:0] Sel_Write,
  input  Write,
  input  [7:0] Data_In,
  input  Clock,
  output [7:0] Data_Out_A,
  output [7:0] Data_Out_B
);

  wire [7:0] reg_bank_1_out_5, reg_bank_1_out_6, reg_bank_1_out_7, reg_bank_1_out_8, reg_bank_1_out_9,
       reg_bank_1_out_10, reg_bank_1_out_11, reg_bank_1_out_12;

  Reg_Bank reg_bank_1 (
    .out_11(reg_bank_1_out_11), .out_12(reg_bank_1_out_12), .out_5(reg_bank_1_out_5),
    .out_6(reg_bank_1_out_6), .out_7(reg_bank_1_out_7), .out_8(reg_bank_1_out_8), .out_9(reg_bank_1_out_9),
    .out_10(reg_bank_1_out_10), .Write(Write), .Sel(Sel_Write), .Clk(Clock), .DATA_IN(Data_In));
  Mux_8_1_8b mux_8_1_8b_1 (
    .D_Out(Data_Out_A), .Sel(Sel_Read_A), .D_0(reg_bank_1_out_5), .D_1(reg_bank_1_out_6),
    .D_2(reg_bank_1_out_7), .D_3(reg_bank_1_out_8), .D_4(reg_bank_1_out_9), .D_5(reg_bank_1_out_10),
    .D_6(reg_bank_1_out_11), .D_7(reg_bank_1_out_12));
  Mux_8_1_8b mux_8_1_8b_2 (
    .D_Out(Data_Out_B), .Sel(Sel_Read_B), .D_0(reg_bank_1_out_5), .D_1(reg_bank_1_out_6),
    .D_2(reg_bank_1_out_7), .D_3(reg_bank_1_out_8), .D_4(reg_bank_1_out_9), .D_5(reg_bank_1_out_10),
    .D_6(reg_bank_1_out_11), .D_7(reg_bank_1_out_12));

  // Notes on the sheet:
  //   The Regster you want to write on
  //   This entire circuit uses the Rising Edge Clock
  //   Since every Register has it's own output in the Register Bank...
  //   ... it's as simple as using the Mux_2_1_8b to selecte the desired Register
  //   ... And.... As the A and B has their own Sel Input, you don't need to care about any complex circuit
endmodule
