// Logisim project Somador.circ as structural Verilog: 3 circuits, main circuit main
module main (
  input  [3:0] A,
  input  [3:0] B,
  output out_3,
  output [3:0] out_4
);

  wire dcm_2_v, dcm_3_v, unidade_1_v;

  DCM dcm_1 (.V(out_3), .R(out_4[3]), .Va(dcm_2_v), .A(A[3]), .B(B[3]));
  DCM dcm_2 (.V(dcm_2_v), .R(out_4[2]), .Va(dcm_3_v), .A(A[2]), .B(B[2]));
  DCM dcm_3 (.V(dcm_3_v), .R(out_4[1]), .Va(unidade_1_v), .A(A[1]), .B(B[1]));
  Unidade unidade_1 (.V(unidade_1_v), .R(out_4[0]), .A(B[0]), .B(A[0]));
endmodule

module Unidade (
  input  A,
  input  B,
  output V,
  output R
);

  wire and_2_out, and_3_out, not_1_out, not_2_out;

  not not_1 (not_1_out, A);
  not not_2 (not_2_out, B);
  and and_1 (V, A, B);
  and and_2 (and_2_out, not_1_out, B);
  and and_3 (and_3_out, A, not_2_out);
  or or_1 (R, and_2_out, and_3_out);
endmodule

module DCM (
  input  Va,
  input  A,
  input  B,
  output V,
  output R
);

  wire and_1_out, and_2_out, and_3_out, and_4_out, and_5_out, and_6_out, and_7_out, not_1_out, not_2_out,
       not_3_out, not_4_out, not_5_out, not_6_out;

  not not_1 (not_1_out, Va);
  not not_2 (not_2_out, B);
  not not_3 (not_3_out, Va);
  not not_4 (not_4_out, A);
  not not_5 (not_5_out, A);
  not not_6 (not_6_out, B);
  and and_1 (and_1_out, A, B);
  and and_2 (and_2_out, Va, B);
  and and_3 (and_3_out, Va, A);
  and and_4 (and_4_out, not_1_out, A, not_2_out);
  and and_5 (and_5_out, not_3_out, not_4_out, B);
  and and_6 (and_6_out, Va, A, B);
  and and_7 (and_7_out, Va, not_5_out, not_6_out);
  or or_1 (V, and_1_out, and_2_out, and_3_out);
  or or_2 (R, and_4_out, and_5_out, and_6_out, and_7_out);
endmodule
